// Logisim project Boba Vending Machine.circ as structural Verilog: 7 circuits, main circuit main
module Money_Input (
  input  _1,
  input  in_2,
  input  _5,
  input  _10,
  input  _25,
  input  _50,
  input  _1_2,
  input  _5_2,
  input  _10_2,
  input  _20,
  output [11:0] out_11,
  output [11:0] out_12
);

  wire comparator_1_gt, comparator_1_lt, n12_bit_super_adder_1_out_11;
  wire [11:0] adder_1_out, n12_bit_super_adder_1_total;

  _12_bit_super_adder u_12_bit_super_adder_1 (
    .in_1({{11{1'b0}}, _1}), .in_2({{9{1'b0}}, _5, 1'b0, _5}), .in_3({{8{1'b0}}, _10, 1'b0, _10, 1'b0}),
    .in_4({{7{1'b0}}, {2{_25}}, 2'b00, _25}), .in_5({{6{1'b0}}, {2{_50}}, 2'b00, _50, 1'b0}),
    .in_6({{5{1'b0}}, {2{_1_2}}, 2'b00, _1_2, 2'b00}), .in_7({3'b000, {5{_5_2}}, 1'b0, _5_2, 2'b00}),
    .in_8({2'b00, {5{_10_2}}, 1'b0, _10_2, 3'b000}), .in_9({1'b0, {5{_20}}, 1'b0, _20, 4'b0000}),
    .Total(n12_bit_super_adder_1_total), .out_11(n12_bit_super_adder_1_out_11));
  Adder #(.width(12)) adder_1 (.a(n12_bit_super_adder_1_total), .b(out_11), .out(adder_1_out));  // open: cin, cout
  Register #(.width(12)) register_1 (
    .D(adder_1_out), .en(comparator_1_lt), .Q(out_11), .clk(n12_bit_super_adder_1_out_11), .clr(in_2));
  Comparator #(.width(12)) comparator_1 (
    .a(out_11), .b(12'h750), .gt(comparator_1_gt), .lt(comparator_1_lt));  // open: eq
  Register #(.width(12)) register_2 (
    .D(n12_bit_super_adder_1_total), .en(comparator_1_gt), .Q(out_12), .clk(n12_bit_super_adder_1_out_11));  // open: clr
endmodule

module main (
  output [2:0] out_1
);

  wire button_1_out, button_2_out, button_3_out, button_4_out, button_5_out, button_6_out, button_7_out,
       button_8_out, button_9_out, button_10_out, button_11_out, button_12_out, clock_1_out, Clr_out;
  wire [3:0] n12_bit_bcd_converter_1_hundreds, n12_bit_bcd_converter_1_ones, n12_bit_bcd_converter_1_tens,
       n12_bit_bcd_converter_1_thousands, n12_bit_bcd_converter_2_hundreds, n12_bit_bcd_converter_2_ones,
       n12_bit_bcd_converter_2_tens, n12_bit_bcd_converter_2_thousands, n12_bit_bcd_converter_3_hundreds,
       n12_bit_bcd_converter_3_ones, n12_bit_bcd_converter_3_tens, n12_bit_bcd_converter_3_thousands,
       n12_bit_bcd_converter_4_hundreds, n12_bit_bcd_converter_4_ones, n12_bit_bcd_converter_4_tens,
       n12_bit_bcd_converter_4_thousands;
  wire [11:0] calc_change_1_out_3, flavor_input_1_price, money_input_1_out_11, money_input_1_out_12;

  LED Not_Enough_Money ();  // open: in
  Button button_1 (.out(button_1_out));
  Button button_2 (.out(button_2_out));
  Button button_3 (.out(button_3_out));
  Button button_4 (.out(button_4_out));
  Button button_5 (.out(button_5_out));
  Button button_6 (.out(button_6_out));
  Button button_7 (.out(button_7_out));
  Button button_8 (.out(button_8_out));
  Button button_9 (.out(button_9_out));
  Button button_10 (.out(button_10_out));
  LED led_1 ();  // open: in
  Button button_11 (.out(button_11_out));
  LED led_2 ();  // open: in
  Button button_12 (.out(button_12_out));
  LED led_3 ();  // open: in
  Money_Input money_input_1 (
    ._1(button_1_out), ._5(button_2_out), ._10(button_3_out), ._25(button_4_out), ._50(button_5_out),
    ._1_2(button_6_out), ._5_2(button_7_out), ._10_2(button_8_out), ._20(button_9_out),
    .out_11(money_input_1_out_11), .in_2(Clr_out), .out_12(money_input_1_out_12));
  Clock clock_1 (.out(clock_1_out));
  Button Clr (.out(Clr_out));
  Button Buy ();  // open: out
  Flavor_Input flavor_input_1 (
    .in_1(button_10_out), .Price(flavor_input_1_price), .Flavor(out_1), .in_2(button_11_out),
    .in_3(button_12_out), .in_4(Clr_out));
  Hex_Digit_Display hex_digit_display_1 (.value(n12_bit_bcd_converter_1_hundreds));  // open: dp
  Hex_Digit_Display hex_digit_display_2 (.value(n12_bit_bcd_converter_1_thousands));  // open: dp
  Hex_Digit_Display hex_digit_display_3 (.value(n12_bit_bcd_converter_1_ones));  // open: dp
  Hex_Digit_Display hex_digit_display_4 (.value(n12_bit_bcd_converter_1_tens));  // open: dp
  _12_bit_BCD_Converter u_12_bit_bcd_converter_1 (
    .Input(money_input_1_out_11), .Thousands(n12_bit_bcd_converter_1_thousands),
    .Hundreds(n12_bit_bcd_converter_1_hundreds), .Tens(n12_bit_bcd_converter_1_tens),
    .Ones(n12_bit_bcd_converter_1_ones));
  calc_change calc_change_1 (.in_1(money_input_1_out_11), .in_2(flavor_input_1_price), .out_3(calc_change_1_out_3));
  Hex_Digit_Display hex_digit_display_5 (.value(n12_bit_bcd_converter_2_thousands));  // open: dp
  Hex_Digit_Display hex_digit_display_6 (.value(n12_bit_bcd_converter_3_thousands));  // open: dp
  Hex_Digit_Display hex_digit_display_7 (.value(n12_bit_bcd_converter_2_tens));  // open: dp
  Hex_Digit_Display hex_digit_display_8 (.value(n12_bit_bcd_converter_2_hundreds));  // open: dp
  _12_bit_BCD_Converter u_12_bit_bcd_converter_2 (
    .Input(calc_change_1_out_3), .Thousands(n12_bit_bcd_converter_2_thousands),
    .Hundreds(n12_bit_bcd_converter_2_hundreds), .Tens(n12_bit_bcd_converter_2_tens),
    .Ones(n12_bit_bcd_converter_2_ones));
  Hex_Digit_Display hex_digit_display_9 (.value(n12_bit_bcd_converter_4_thousands));  // open: dp
  Hex_Digit_Display hex_digit_display_10 (.value(n12_bit_bcd_converter_4_hundreds));  // open: dp
  Hex_Digit_Display hex_digit_display_11 (.value(n12_bit_bcd_converter_3_hundreds));  // open: dp
  Hex_Digit_Display hex_digit_display_12 (.value(n12_bit_bcd_converter_3_tens));  // open: dp
  _12_bit_BCD_Converter u_12_bit_bcd_converter_3 (
    .Input(flavor_input_1_price), .Thousands(n12_bit_bcd_converter_3_thousands),
    .Hundreds(n12_bit_bcd_converter_3_hundreds), .Tens(n12_bit_bcd_converter_3_tens),
    .Ones(n12_bit_bcd_converter_3_ones));
  Hex_Digit_Display hex_digit_display_13 (.value(n12_bit_bcd_converter_2_ones));  // open: dp
  Hex_Digit_Display hex_digit_display_14 (.value(n12_bit_bcd_converter_4_ones));  // open: dp
  Hex_Digit_Display hex_digit_display_15 (.value(n12_bit_bcd_converter_4_tens));  // open: dp
  _12_bit_BCD_Converter u_12_bit_bcd_converter_4 (
    .Input(money_input_1_out_12), .Thousands(n12_bit_bcd_converter_4_thousands),
    .Hundreds(n12_bit_bcd_converter_4_hundreds), .Tens(n12_bit_bcd_converter_4_tens),
    .Ones(n12_bit_bcd_converter_4_ones));
  Hex_Digit_Display hex_digit_display_16 (.value(n12_bit_bcd_converter_3_ones));  // open: dp
  LED led_4 (.in(out_1[0]));
  LED led_5 (.in(out_1[1]));
  LED led_6 (.in(out_1[2]));

  // Notes on the sheet:
  //   Flavor
  //   Money Input
  //   Total:
endmodule

module Flavor_Input (
  input  in_1,
  input  in_2,
  input  in_3,
  input  in_4,
  output [11:0] Price,
  output [2:0] Flavor
);

  wire comparator_1_eq, not_1_out;

  Comparator #(.width(3)) comparator_1 (.a({in_3, in_2, in_1}), .b(3'b000), .eq(comparator_1_eq));  // open: gt, lt
  not not_1 (not_1_out, comparator_1_eq);
  Register #(.width(3)) register_1 (.D({in_3, in_2, in_1}), .en(not_1_out), .Q(Flavor), .clk(not_1_out), .clr(in_4));
  Flavor_State flavor_state_1 (
    .a(Flavor[0]), .b(Flavor[1]), .c(Flavor[2]), .x(Price[11]), .y(Price[10]), .z(Price[9]), .u(Price[8]),
    .v(Price[7]), .w(Price[6]), .s(Price[5]), .t(Price[4]), .x2(Price[3]), .x3(Price[2]), .x4(Price[1]),
    .x5(Price[0]));
endmodule

module Flavor_State (
  input  a,
  input  b,
  input  c,
  output x,
  output y,
  output z,
  output u,
  output v,
  output w,
  output s,
  output t,
  output x2,
  output x3,
  output x4,
  output x5
);

  wire and_2_out, and_3_out, and_5_out, and_6_out, and_7_out, and_10_out, and_11_out, and_12_out, and_13_out,
       not_1_out, not_2_out, not_3_out, not_4_out, not_5_out, not_6_out, not_7_out, not_8_out, not_9_out,
       not_10_out, not_11_out, not_12_out, not_13_out, not_14_out, not_15_out, not_16_out, not_17_out,
       not_18_out, not_19_out, not_20_out, not_21_out, not_22_out, not_23_out, not_24_out, not_25_out,
       not_26_out, not_27_out, not_28_out;

  not not_1 (not_1_out, a);
  not not_2 (not_2_out, b);
  not not_3 (not_3_out, a);
  not not_4 (not_4_out, c);
  not not_5 (not_5_out, b);
  not not_6 (not_6_out, c);
  not not_7 (not_7_out, a);
  not not_8 (not_8_out, c);
  not not_9 (not_9_out, a);
  not not_10 (not_10_out, b);
  not not_11 (not_11_out, a);
  not not_12 (not_12_out, c);
  not not_13 (not_13_out, b);
  not not_14 (not_14_out, c);
  not not_15 (not_15_out, b);
  not not_16 (not_16_out, c);
  not not_17 (not_17_out, a);
  not not_18 (not_18_out, b);
  not not_19 (not_19_out, a);
  not not_20 (not_20_out, b);
  not not_21 (not_21_out, b);
  not not_22 (not_22_out, c);
  not not_23 (not_23_out, a);
  not not_24 (not_24_out, c);
  not not_25 (not_25_out, b);
  not not_26 (not_26_out, c);
  not not_27 (not_27_out, b);
  not not_28 (not_28_out, c);
  and and_1 (y, not_1_out, not_2_out, c);
  and and_2 (and_2_out, not_3_out, b, not_4_out);
  and and_3 (and_3_out, a, not_5_out, not_6_out);
  and and_4 (u, not_7_out, b, not_8_out);
  and and_5 (and_5_out, not_9_out, not_10_out, c);
  and and_6 (and_6_out, not_11_out, b, not_12_out);
  and and_7 (and_7_out, a, not_13_out, not_14_out);
  and and_8 (w, a, not_15_out, not_16_out);
  and and_9 (s, not_17_out, not_18_out, c);
  and and_10 (and_10_out, not_19_out, not_20_out, c);
  and and_11 (and_11_out, a, not_21_out, not_22_out);
  and and_12 (and_12_out, not_23_out, b, not_24_out);
  and and_13 (and_13_out, a, not_25_out, not_26_out);
  and and_14 (x5, a, not_27_out, not_28_out);
  or or_1 (z, and_2_out, and_3_out);
  or or_2 (v, and_5_out, and_6_out, and_7_out);
  or or_3 (t, and_10_out, and_11_out);
  or or_4 (x3, and_12_out, and_13_out);

  assign x = 1'b0;
  assign x2 = 1'b0;
  assign x4 = 1'b0;
endmodule

// Super adder
module _12_bit_super_adder (
  input  [11:0] in_1,
  input  [11:0] in_2,
  input  [11:0] in_3,
  input  [11:0] in_4,
  input  [11:0] in_5,
  input  [11:0] in_6,
  input  [11:0] in_7,
  input  [11:0] in_8,
  input  [11:0] in_9,
  output [11:0] Total,
  output out_11
);

  wire [11:0] adder_1_out, adder_2_out, adder_3_out, adder_4_out, adder_5_out, adder_6_out, adder_7_out;

  Adder #(.width(12)) adder_1 (.a(in_1), .b(in_2), .out(adder_1_out));  // open: cin, cout
  Adder #(.width(12)) adder_2 (.a(in_3), .b(in_4), .out(adder_2_out));  // open: cin, cout
  Adder #(.width(12)) adder_3 (.a(in_5), .b(in_6), .out(adder_3_out));  // open: cin, cout
  Adder #(.width(12)) adder_4 (.a(in_7), .b(in_8), .out(adder_4_out));  // open: cin, cout
  Adder #(.width(12)) adder_5 (.a(adder_1_out), .b(adder_2_out), .out(adder_5_out));  // open: cin, cout
  Adder #(.width(12)) adder_6 (.a(adder_3_out), .b(adder_4_out), .out(adder_6_out));  // open: cin, cout
  Adder #(.width(12)) adder_7 (.a(adder_5_out), .b(adder_6_out), .out(adder_7_out));  // open: cin, cout
  Adder #(.width(12)) adder_8 (.a(adder_7_out), .b(in_9), .out(Total));  // open: cin, cout
  Comparator #(.width(12)) comparator_1 (.a(Total), .b({12{1'b0}}), .gt(out_11));  // open: eq, lt
endmodule

module _12_bit_BCD_Converter (
  input  [11:0] Input,
  output [3:0] Thousands,
  output [3:0] Hundreds,
  output [3:0] Tens,
  output [3:0] Ones
);

  wire comparator_1_lt, comparator_2_lt, comparator_3_lt, comparator_4_lt, comparator_5_lt, comparator_6_lt,
       comparator_7_lt, comparator_8_lt, comparator_9_lt, comparator_10_lt, comparator_11_lt,
       comparator_12_lt, comparator_13_lt, comparator_14_lt, comparator_15_lt, comparator_16_lt,
       comparator_17_lt, comparator_18_lt, comparator_19_lt;
  wire [0:0] adder_1_out_2, adder_2_out, adder_4_out_2;
  wire [1:1] not_1_out, not_2_out, not_3_out, not_4_out, not_5_out, not_6_out, not_7_out, not_8_out,
       not_9_out, not_10_out, not_11_out, not_12_out, not_13_out, not_14_out, not_15_out, not_16_out,
       not_17_out, not_18_out, not_19_out;
  wire [2:0] adder_11_out_2, adder_14_out_2;
  wire [3:0] adder_14_out, adder_16_out;
  wire [3:1] adder_1_out, adder_2_out_3, adder_5_out, adder_11_out, adder_12_out, adder_13_out;
  wire [11:0] adder_3_out, adder_4_out, adder_8_out, adder_15_out, adder_17_out, adder_18_out, adder_19_out;
  wire [11:1] adder_7_out;
  wire [11:3] adder_5_out_2;
  wire [11:4] adder_2_out_2, adder_6_out, adder_9_out, adder_10_out, adder_11_out_3, adder_12_out_2,
       adder_13_out_2, adder_14_out_3, adder_16_out_2;
  wire [11:11] adder_1_out_3;

  not not_1 (not_1_out[1], comparator_1_lt);
  not not_2 (not_2_out[1], comparator_2_lt);
  not not_3 (not_3_out[1], comparator_3_lt);
  not not_4 (not_4_out[1], comparator_4_lt);
  not not_5 (not_5_out[1], comparator_5_lt);
  not not_6 (not_6_out[1], comparator_6_lt);
  Comparator #(.width(12), .mode("unsigned")) comparator_1 (
    .a({{8{1'b0}}, adder_17_out[2:0], Input[4]}), .b(12'h5), .lt(comparator_1_lt));  // open: gt, eq
  Adder #(.width(12)) adder_1 (
    .a({{8{1'b0}}, adder_17_out[2:0], Input[4]}), .b({{10{1'b0}}, {2{not_1_out[1]}}}),
    .out({{8{adder_1_out_3[11]}}, adder_1_out_2[0], adder_1_out}));  // open: cin, cout
  Comparator #(.width(12), .mode("unsigned")) comparator_2 (
    .a({{8{1'b0}}, adder_18_out[2:0], adder_1_out_2[0]}), .b(12'h5), .lt(comparator_2_lt));  // open: gt, eq
  Adder #(.width(12)) adder_2 (
    .a({{8{1'b0}}, adder_18_out[2:0], adder_1_out_2[0]}), .b({{10{1'b0}}, {2{not_2_out[1]}}}),
    .out({adder_2_out_2, adder_2_out[0], adder_2_out_3}));  // open: cin, cout
  Comparator #(.width(12), .mode("unsigned")) comparator_3 (
    .a({{8{1'b0}}, adder_1_out, Input[3]}), .b(12'h5), .lt(comparator_3_lt));  // open: gt, eq
  Adder #(.width(12)) adder_3 (
    .a({{8{1'b0}}, adder_1_out, Input[3]}), .b({{10{1'b0}}, {2{not_3_out[1]}}}), .out(adder_3_out));  // open: cin, cout
  Comparator #(.width(12), .mode("unsigned")) comparator_4 (
    .a({{8{1'b0}}, adder_2_out_3, adder_3_out[3]}), .b(12'h5), .lt(comparator_4_lt));  // open: gt, eq
  Adder #(.width(12)) adder_4 (
    .a({{8{1'b0}}, adder_2_out_3, adder_3_out[3]}), .b({{10{1'b0}}, {2{not_4_out[1]}}}),
    .out({adder_4_out[11:4], adder_4_out_2[0], adder_4_out[2:0]}));  // open: cin, cout
  Comparator #(.width(12), .mode("unsigned")) comparator_5 (
    .a({{8{1'b0}}, adder_3_out[2:0], Input[2]}), .b(12'h5), .lt(comparator_5_lt));  // open: gt, eq
  Adder #(.width(12)) adder_5 (
    .a({{8{1'b0}}, adder_3_out[2:0], Input[2]}), .b({{10{1'b0}}, {2{not_5_out[1]}}}),
    .out({adder_5_out_2, adder_5_out}));  // open: cin, cout
  Comparator #(.width(12), .mode("unsigned")) comparator_6 (
    .a({{8{1'b0}}, adder_8_out[2:0], adder_4_out_2[0]}), .b(12'h5), .lt(comparator_6_lt));  // open: gt, eq
  Adder #(.width(12)) adder_6 (
    .a({{8{1'b0}}, adder_8_out[2:0], adder_4_out_2[0]}), .b({{10{1'b0}}, {2{not_6_out[1]}}}),
    .out({adder_6_out, Thousands[0], Hundreds[3:1]}));  // open: cin, cout
  not not_7 (not_7_out[1], comparator_7_lt);
  not not_8 (not_8_out[1], comparator_8_lt);
  not not_9 (not_9_out[1], comparator_9_lt);
  not not_10 (not_10_out[1], comparator_10_lt);
  not not_11 (not_11_out[1], comparator_11_lt);
  not not_12 (not_12_out[1], comparator_12_lt);
  not not_13 (not_13_out[1], comparator_13_lt);
  not not_14 (not_14_out[1], comparator_14_lt);
  not not_15 (not_15_out[1], comparator_15_lt);
  not not_16 (not_16_out[1], comparator_16_lt);
  not not_17 (not_17_out[1], comparator_17_lt);
  not not_18 (not_18_out[1], comparator_18_lt);
  not not_19 (not_19_out[1], comparator_19_lt);
  Comparator #(.width(12), .mode("unsigned")) comparator_7 (
    .a({{11{1'b0}}, adder_19_out[3]}), .b(12'h5), .lt(comparator_7_lt));  // open: gt, eq
  Adder #(.width(12)) adder_7 (
    .a({{11{1'b0}}, adder_19_out[3]}), .b({{10{1'b0}}, {2{not_7_out[1]}}}), .out({adder_7_out, Thousands[2]}));  // open: cin, cout
  Comparator #(.width(12), .mode("unsigned")) comparator_8 (
    .a({{8{1'b0}}, adder_19_out[2:0], adder_2_out[0]}), .b(12'h5), .lt(comparator_8_lt));  // open: gt, eq
  Adder #(.width(12)) adder_8 (
    .a({{8{1'b0}}, adder_19_out[2:0], adder_2_out[0]}), .b({{10{1'b0}}, {2{not_8_out[1]}}}),
    .out({adder_8_out[11:4], Thousands[1], adder_8_out[2:0]}));  // open: cin, cout
  Comparator #(.width(12), .mode("unsigned")) comparator_9 (
    .a({{8{1'b0}}, adder_4_out[2:0], adder_5_out_2[3]}), .b(12'h5), .lt(comparator_9_lt));  // open: gt, eq
  Adder #(.width(12)) adder_9 (
    .a({{8{1'b0}}, adder_4_out[2:0], adder_5_out_2[3]}), .b({{10{1'b0}}, {2{not_9_out[1]}}}),
    .out({adder_9_out, Hundreds[0], Tens[3:1]}));  // open: cin, cout
  Comparator #(.width(12), .mode("unsigned")) comparator_10 (
    .a({{8{1'b0}}, adder_5_out, Input[1]}), .b(12'h5), .lt(comparator_10_lt));  // open: gt, eq
  Adder #(.width(12)) adder_10 (
    .a({{8{1'b0}}, adder_5_out, Input[1]}), .b({{10{1'b0}}, {2{not_10_out[1]}}}),
    .out({adder_10_out, Tens[0], Ones[3:1]}));  // open: cin, cout
  Comparator #(.width(12), .mode("unsigned")) comparator_11 (
    .a({{9{1'b0}}, Input[11:9]}), .b(12'h5), .lt(comparator_11_lt));  // open: gt, eq
  Adder #(.width(12)) adder_11 (
    .a({{9{1'b0}}, Input[11:9]}), .b({{10{1'b0}}, {2{not_11_out[1]}}}),
    .out({adder_11_out_3, adder_11_out_2[2], adder_11_out}));  // open: cin, cout
  Comparator #(.width(12), .mode("unsigned")) comparator_12 (
    .a({{8{1'b0}}, adder_11_out, Input[8]}), .b(12'h5), .lt(comparator_12_lt));  // open: gt, eq
  Adder #(.width(12)) adder_12 (
    .a({{8{1'b0}}, adder_11_out, Input[8]}), .b({{10{1'b0}}, {2{not_12_out[1]}}}),
    .out({adder_12_out_2, adder_11_out_2[1], adder_12_out}));  // open: cin, cout
  Comparator #(.width(12), .mode("unsigned")) comparator_13 (
    .a({{8{1'b0}}, adder_12_out, Input[7]}), .b(12'h5), .lt(comparator_13_lt));  // open: gt, eq
  Adder #(.width(12)) adder_13 (
    .a({{8{1'b0}}, adder_12_out, Input[7]}), .b({{10{1'b0}}, {2{not_13_out[1]}}}),
    .out({adder_13_out_2, adder_11_out_2[0], adder_13_out}));  // open: cin, cout
  Comparator #(.width(12), .mode("unsigned")) comparator_14 (
    .a({{9{1'b0}}, adder_11_out_2}), .b(12'h5), .lt(comparator_14_lt));  // open: gt, eq
  Adder #(.width(12)) adder_14 (
    .a({{9{1'b0}}, adder_11_out_2}), .b({{10{1'b0}}, {2{not_14_out[1]}}}),
    .out({adder_14_out_3, adder_14_out_2[2], adder_14_out[3:1]}));  // open: cin, cout
  Comparator #(.width(12), .mode("unsigned")) comparator_15 (
    .a({{8{1'b0}}, adder_13_out, Input[6]}), .b(12'h5), .lt(comparator_15_lt));  // open: gt, eq
  Adder #(.width(12)) adder_15 (
    .a({{8{1'b0}}, adder_13_out, Input[6]}), .b({{10{1'b0}}, {2{not_15_out[1]}}}),
    .out({adder_15_out[11:4], adder_14_out[0], adder_15_out[2:0]}));  // open: cin, cout
  Comparator #(.width(12), .mode("unsigned")) comparator_16 (
    .a({{8{1'b0}}, adder_14_out}), .b(12'h5), .lt(comparator_16_lt));  // open: gt, eq
  Adder #(.width(12)) adder_16 (
    .a({{8{1'b0}}, adder_14_out}), .b({{10{1'b0}}, {2{not_16_out[1]}}}),
    .out({adder_16_out_2, adder_14_out_2[1], adder_16_out[3:1]}));  // open: cin, cout
  Comparator #(.width(12), .mode("unsigned")) comparator_17 (
    .a({{8{1'b0}}, adder_15_out[2:0], Input[5]}), .b(12'h5), .lt(comparator_17_lt));  // open: gt, eq
  Adder #(.width(12)) adder_17 (
    .a({{8{1'b0}}, adder_15_out[2:0], Input[5]}), .b({{10{1'b0}}, {2{not_17_out[1]}}}),
    .out({adder_17_out[11:4], adder_16_out[0], adder_17_out[2:0]}));  // open: cin, cout
  Comparator #(.width(12), .mode("unsigned")) comparator_18 (
    .a({{8{1'b0}}, adder_16_out}), .b(12'h5), .lt(comparator_18_lt));  // open: gt, eq
  Adder #(.width(12)) adder_18 (
    .a({{8{1'b0}}, adder_16_out}), .b({{10{1'b0}}, {2{not_18_out[1]}}}),
    .out({{8{adder_18_out[11]}}, adder_14_out_2[0], adder_18_out[2:0]}));  // open: cin, cout
  Comparator #(.width(12), .mode("unsigned")) comparator_19 (
    .a({{9{1'b0}}, adder_14_out_2}), .b(12'h5), .lt(comparator_19_lt));  // open: gt, eq
  Adder #(.width(12)) adder_19 (
    .a({{9{1'b0}}, adder_14_out_2}), .b({{10{1'b0}}, {2{not_19_out[1]}}}), .out(adder_19_out));  // open: cin, cout
  Hex_Digit_Display hex_digit_display_1 (.value({1'b0, Thousands[2:0]}));  // open: dp
  Hex_Digit_Display hex_digit_display_2 (.value(Hundreds));  // open: dp
  Hex_Digit_Display hex_digit_display_3 (.value(Tens));  // open: dp
  Hex_Digit_Display hex_digit_display_4 (.value({Ones[3:1], Input[0]}));  // open: dp

  assign Ones[0] = Input[0];
  assign Thousands[3] = 1'b0;
  // also tied to GND on the sheet: {adder_1_out_3[11], adder_18_out[11]}

  // Notes on the sheet:
  //   Tens
  //   Hundreds
  //   Hundreds
  //   Thousands
  //   Thousands
  //   Ones
  //   Ones
  //   Ones
  //   Tens
  //   Ones
  //   Tens
  //   Ones
  //   Tens
  //   Ones
  //   Ones
  //   Tens
  //   Tens
  //   Hundreds
  //   Hundreds
  //   Ones
  //   Ones
  //   Tens
  //   Tens
  //   Ones
  //   Ones
endmodule

module calc_change (
  input  [11:0] in_1,
  input  [11:0] in_2,
  output [11:0] out_3
);

  Subtractor #(.width(12)) subtractor_1 (.a(in_1), .b(in_2), .out(out_3));  // open: bin, bout
endmodule
